// Digital circuit programCounter.dig as structural Verilog
module programCounter (
  input  [3:0] Load,
  input  Increment,
  output [3:0] Address_bus,
  output Out_of_range
);

  wire [3:0] _4bit_full_adder_1_sum;

  _4bit_full_adder _4bit_full_adder_1 (
    .zero(1'b0), .A(Load), .B({3'b000, Increment}), .sum(_4bit_full_adder_1_sum), .overflow(Out_of_range));
  _4_bit_register _4_bit_register_1 (.Data(_4bit_full_adder_1_sum), .C(Increment), .Out(Address_bus));
endmodule
